# Fritzing sketch fire_detection_robot (saved by Fritzing 1.0.4)
breadboards: 1

parts:
  HC-SR04_Sensor_Left = HC-SR04 Ultrasonic Distance Sensor
  MQ-2 = MQ-2 Gas Sensor  # not connected
  L298N = L298_BRIDGE_DRIVER [package=powerso20]  # not connected
  DC_Motor_Left = gear-motor  # not connected
  DC_Motor_Right = gear-motor  # not connected
  GY-NEO6MV3 = SUP500F [package=sup500f]  # not connected
  SX1278 = Osoyoo SX1278-ra-02  # not connected
  ANT1 = Antenna  # not connected
  DC-DC_Converter_5V = RioRand LM2596  # not connected
  DC-DC_Converter_6V = RioRand LM2596  # not connected
  J1 = Basic Servo  # not connected
  Εξάρτημα2 = INA 260  # not connected
  microSD1 = MicroSD Card Module  # not connected
  HC-SR04_Sensor_Front = HC-SR04 Ultrasonic Distance Sensor
  HC-SR04_Sensor_Right = HC-SR04 Ultrasonic Distance Sensor
  Εξάρτημα3 = Arduino Mega ADK (Rev3)

nets:
  N1: HC-SR04_Sensor_Left.TRIG, Εξάρτημα3.D30
  N2: HC-SR04_Sensor_Left.ECHO, Εξάρτημα3.D31
  GND: HC-SR04_Sensor_Left.GND, HC-SR04_Sensor_Front.GND, HC-SR04_Sensor_Right.GND
  N3: HC-SR04_Sensor_Front.TRIG, Εξάρτημα3.D32
  N4: HC-SR04_Sensor_Front.ECHO, Εξάρτημα3.D33
  N5: HC-SR04_Sensor_Right.TRIG, Εξάρτημα3.D34
  N6: HC-SR04_Sensor_Right.ECHO, Εξάρτημα3.D35

notes:
  GND:Black
  VCC: Red
  RX: Yellow
  TX: Green
  GND:Black
  VCC: Red (+5V)
  Trig: Yellow (34)
  Echo: Green (35)
  GND:Black
  VCC: Red (+5V)
  Trig: Yellow (30)
  Echo: Green (31)
  GND:Black
  VCC: Red (+5V)
  Trig: Yellow (32)
  Echo: Green (33)

custom parts:
  MQ-2 Gas Sensor: MQ-2 Gas Sensor module of ZHIYU Sensor Kit
  Osoyoo SX1278-ra-02: Osoyoo Long Distance wireless transceiver Uart LoRa Module.
  INA 260: Rev. B, add copy
